# Fritzing sketch PCB Entier (saved by Fritzing 0.9.1b)
circuit board: 2.73cm x 1.1cm
breadboards: 1

parts:
  C3 = Ceramic Capacitor [capacitance=100nF package="100 mil [THT, multilayer]"]
  C4 = Ceramic Capacitor [capacitance=100nF package="100 mil [THT, multilayer]"]
  IC2 = SO16 [chip_label=IC package=SO]
  R6 = Resistor [tolerance=±5% resistance=220 package="0603 [SMD]"]  # not connected
  R7 = Resistor [tolerance=±5% resistance=220 package="0603 [SMD]"]  # not connected
  R8 = Resistor [tolerance=±5% resistance=220 package="0603 [SMD]"]  # not connected

nets:
  N1: C3.0, C4.0, IC2.1, IC2.13
  N2: C3.1, C4.1, IC2.16
