# Fritzing sketch PCB Led Drivers horizontaux (saved by Fritzing 0.9.1b)
circuit board: 3.25306cm x 19.986cm
breadboards: 1

parts:
  LED4 = RGB LED (com. anode, rbg) [package="5 mm [THT]"]
  LED18 = RGB LED (com. anode, rbg) [package="5 mm [THT]"]
  LED19 = RGB LED (com. anode, rbg) [package="5 mm [THT]"]
  J15 = female pin header, 2 pins [form="♀ (female)"]
  J16 = female pin header, 3 pins [form="♀ (female)"]
  R40 = Resistor [tolerance=±5% resistance=220 package=THT]
  IC1 = IC, DIP package, 16 pins [chip_label=IC]
  C1 = Tantalum Capacitor [capacitance=1μF package="100 mil [THT, tantalum]"]
  C2 = Ceramic Capacitor [capacitance=100nF package="100 mil [THT, multilayer]"]
  LED21 = RGB LED (com. anode, rbg) [package="5 mm [THT]"]
  LED22 = RGB LED (com. anode, rbg) [package="5 mm [THT]"]  # not connected
  LED23 = RGB LED (com. anode, rbg) [package="5 mm [THT]"]
  LED24 = RGB LED (com. anode, rbg) [package="5 mm [THT]"]
  R41 = Resistor [tolerance=±5% resistance=220 package=THT]
  IC2 = IC, DIP package, 16 pins [chip_label=IC]
  C3 = Tantalum Capacitor [capacitance=1μF package="100 mil [THT, tantalum]"]
  C4 = Ceramic Capacitor [capacitance=100nF package="100 mil [THT, multilayer]"]

nets:
  N1: LED4.red_cathode, IC1.pin5
  N2: LED4.common_anode, LED18.common_anode
  N3: LED4.blue_cathode, IC1.pin6
  N4: LED4.green_cathode, IC1.pin7
  N5: LED18.red_cathode, IC1.pin8
  N6: LED18.blue_cathode, IC1.pin9
  N7: LED18.green_cathode, IC1.pin10
  N8: LED19.red_cathode, IC1.pin11
  N9: LED19.blue_cathode, IC1.pin12
  N10: J15.pin1, IC1.pin16, C1.-, C2.0
  N11: J15.pin2, R40.Pin_1, IC1.pin1, IC1.pin13, C1.+, C2.1
  N12: J16.pin1, IC1.pin2
  N13: J16.pin2, IC1.pin3
  N14: J16.pin3, IC1.pin4
  N15: R40.Pin_0, IC1.pin15
  N16: IC1.pin14, IC2.pin2
  N17: LED21.red_cathode, IC2.pin11
  N18: LED21.blue_cathode, IC2.pin12
  N19: LED23.red_cathode, IC2.pin8
  N20: LED23.common_anode, LED24.common_anode
  N21: LED23.blue_cathode, IC2.pin9
  N22: LED23.green_cathode, IC2.pin10
  N23: LED24.red_cathode, IC2.pin5
  N24: LED24.blue_cathode, IC2.pin6
  N25: LED24.green_cathode, IC2.pin7
  N26: R41.Pin_0, IC2.pin15
  N27: R41.Pin_1, IC2.pin1, IC2.pin13
  N28: C3.-, C4.0
  N29: C3.+, C4.1
